# Fritzing sketch piscine (saved by Fritzing 0.9.3b)
breadboards: 1

parts:
  Composant1 = Arduino Ethernet Shield (Rev3)
  Composant2 = Arduino Uno (Rev3) - ICSP
  Squix1 = OLED 0.96" 128x64 I2C SSD1306
  Composant3 = Adafruit DS3231 [part_number="Adafruit #3013"]
  R1 = Resistor [tolerance=±5% resistance=10k package=THT]
  R2 = Resistor [tolerance=±5% resistance=10k package=THT]
  S1 = PH meter [package=THT]

nets:
  N1: Composant1.ICSP_MISO, Composant2.ICSP_MISO
  5V: Composant1.5V, Composant2.5V, Squix1.VCC, Composant3.Vin, R1.Pin_1, R2.Pin_1, S1.pin2
  N2: Composant1.ICSP_SCK, Composant2.ICSP_SCK
  N3: Composant1.ICSP_MOSI, Composant2.ICSP_MOSI
  N4: Composant1.RESET, Composant2.RESET
  GND: Composant1.GND, Composant2.GND, Squix1.GND, Composant3.GND, S1.pin3
  N5: Composant1.ETH_CS, Composant2.D10_PWM/SS
  N6: Composant1.PWM_D11, Composant2.D11_PWM/MOSI
  N7: Composant1.SPI/D12, Composant2.D12/MISO
  N8: Composant1.SPI/D13, Composant2.D13/SCK
  N9: Composant1.SDCS, Composant2.D4
  N10: Composant2.A3, S1.pin1
  N11: Composant2.A4/SDA, Squix1.SCA, Composant3.SDA, R2.Pin_0
  N12: Composant2.A5/SCL, Squix1.SCL, Composant3.SCL, R1.Pin_0

custom parts:
  Adafruit DS3231: The datasheet for the DS3231 explains that this part is an "Extremely Accurate I²C-Integrated RTC/TCXO/Crystal". And, hey, it does exactly what it says on the tin! This Real Time Clock (RTC) is the most precise you can get in a small, low power package. Most RTCs use an external 32kHz timing crystal that is used to keep time with low current draw. And that's all well and good, but those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
